# Fritzing sketch ps2toatarijoy (saved by Fritzing 0.9.3b)

parts:
  ARDUINO = Arduino Uno (Rev3)
  PS2X_Controller_port = Header 10 [package=1x10-2mm-smd]
  Atari_Joy_Connector = DB9 Connector [package=db9]

nets:
  N1: ARDUINO.D10_PWM/SS, PS2X_Controller_port.7
  N2: ARDUINO.D11_PWM/MOSI, PS2X_Controller_port.6
  N3: ARDUINO.D12/MISO, PS2X_Controller_port.2
  N4: ARDUINO.D13/SCK, PS2X_Controller_port.1
  N5: ARDUINO.D2, Atari_Joy_Connector.1
  N6: ARDUINO.D4, Atari_Joy_Connector.6
  N7: ARDUINO.D5_PWM, Atari_Joy_Connector.7
  N8: ARDUINO.D6_PWM, Atari_Joy_Connector.8
  N9: ARDUINO.D7, Atari_Joy_Connector.9
  N10: ARDUINO.3V3, PS2X_Controller_port.5
  N11: ARDUINO.GND, PS2X_Controller_port.4
  N12: ARDUINO.VIN, Atari_Joy_Connector.2
